// Logisim project ejerA.circ as structural Verilog: 8 circuits, main circuit main
module main (
  input  c0,
  input  c1,
  input  Z,
  input  [7:0] X,
  input  [7:0] W
);

  wire ca1_mult_sum_1_out_6, ca1_mult_sum_1_out_7, ca1_mult_sum_1_out_8, ca1_mult_sum_1_out_9,
       ca1_mult_sum_1_out_10, ca1_mult_sum_1_out_11, ca1_mult_sum_1_out_12, ca1_mult_sum_1_out_13,
       ca1_mult_sum_1_out_14, ca1_mult_sum_1_out_15, ca1_mult_sum_1_out_16, ca1_mult_sum_1_out_17,
       ca1_mult_sum_1_out_18, ca1_mult_sum_1_out_19, ca1_mult_sum_1_out_20, ca1_mult_sum_1_out_21,
       ca1_mult_sum_1_out_22, ca1_mult_sum_1_out_23;

  _7_Segment_Display u_7_segment_display_1 (
    .f(ca1_mult_sum_1_out_6), .a(ca1_mult_sum_1_out_6), .b(ca1_mult_sum_1_out_7), .e(ca1_mult_sum_1_out_6),
    .d(ca1_mult_sum_1_out_6), .c(ca1_mult_sum_1_out_7));  // open: g, dp
  _7_Segment_Display u_7_segment_display_2 (
    .f(ca1_mult_sum_1_out_8), .a(ca1_mult_sum_1_out_8), .b(ca1_mult_sum_1_out_9), .e(ca1_mult_sum_1_out_8),
    .d(ca1_mult_sum_1_out_8), .c(ca1_mult_sum_1_out_9));  // open: g, dp
  _7_Segment_Display u_7_segment_display_3 (
    .f(ca1_mult_sum_1_out_12), .a(ca1_mult_sum_1_out_12), .b(ca1_mult_sum_1_out_13),
    .e(ca1_mult_sum_1_out_12), .d(ca1_mult_sum_1_out_12), .c(ca1_mult_sum_1_out_13));  // open: g, dp
  _7_Segment_Display u_7_segment_display_4 (
    .f(ca1_mult_sum_1_out_10), .a(ca1_mult_sum_1_out_10), .b(ca1_mult_sum_1_out_11),
    .e(ca1_mult_sum_1_out_10), .d(ca1_mult_sum_1_out_10), .c(ca1_mult_sum_1_out_11));  // open: g, dp
  CA1___mult___sum ca1_mult_sum_1 (
    .in_1(c0), .in_2(c1), .Z(Z), .X(X), .W(W), .out_6(ca1_mult_sum_1_out_6), .out_7(ca1_mult_sum_1_out_7),
    .out_8(ca1_mult_sum_1_out_8), .out_9(ca1_mult_sum_1_out_9), .out_10(ca1_mult_sum_1_out_10),
    .out_11(ca1_mult_sum_1_out_11), .out_12(ca1_mult_sum_1_out_12), .out_13(ca1_mult_sum_1_out_13),
    .out_14(ca1_mult_sum_1_out_14), .out_15(ca1_mult_sum_1_out_15), .out_16(ca1_mult_sum_1_out_16),
    .out_17(ca1_mult_sum_1_out_17), .out_18(ca1_mult_sum_1_out_18), .out_19(ca1_mult_sum_1_out_19),
    .out_20(ca1_mult_sum_1_out_20), .out_21(ca1_mult_sum_1_out_21), .out_22(ca1_mult_sum_1_out_22),
    .out_23(ca1_mult_sum_1_out_23));
  _7_Segment_Display u_7_segment_display_5 (
    .f(ca1_mult_sum_1_out_14), .a(ca1_mult_sum_1_out_14), .b(ca1_mult_sum_1_out_15),
    .e(ca1_mult_sum_1_out_14), .d(ca1_mult_sum_1_out_14), .c(ca1_mult_sum_1_out_15));  // open: g, dp
  _7_Segment_Display u_7_segment_display_6 (
    .f(ca1_mult_sum_1_out_16), .a(ca1_mult_sum_1_out_16), .b(ca1_mult_sum_1_out_17),
    .e(ca1_mult_sum_1_out_16), .d(ca1_mult_sum_1_out_16), .c(ca1_mult_sum_1_out_17));  // open: g, dp
  _7_Segment_Display u_7_segment_display_7 (
    .f(ca1_mult_sum_1_out_20), .a(ca1_mult_sum_1_out_20), .b(ca1_mult_sum_1_out_21),
    .e(ca1_mult_sum_1_out_20), .d(ca1_mult_sum_1_out_20), .c(ca1_mult_sum_1_out_21));  // open: g, dp
  _7_Segment_Display u_7_segment_display_8 (
    .f(ca1_mult_sum_1_out_18), .a(ca1_mult_sum_1_out_18), .b(ca1_mult_sum_1_out_19),
    .e(ca1_mult_sum_1_out_18), .d(ca1_mult_sum_1_out_18), .c(ca1_mult_sum_1_out_19));  // open: g, dp
  _7_Segment_Display u_7_segment_display_9 (
    .f(ca1_mult_sum_1_out_22), .a(ca1_mult_sum_1_out_22), .b(ca1_mult_sum_1_out_23),
    .e(ca1_mult_sum_1_out_22), .d(ca1_mult_sum_1_out_22), .c(ca1_mult_sum_1_out_23));  // open: g, dp

  // Notes on the sheet:
  //   Referencias (c0 / c1): 
  //   0 0: indiferente
  //   0 1: CA1 (X)
  //   1 0: multiplicadorbit (X * z)
  //   1 1: sumtot8 (W + X)
endmodule

module led (
  input  a,
  input  encendido___apagado,
  output s2,
  output s1
);

  wire controlled_buffer_2_out;

  assign s2 = encendido___apagado ? 1'b1 : 1'bz;  // Controlled_Buffer controlled_buffer_1
  assign controlled_buffer_2_out = encendido___apagado ? a : 1'bz;  // Controlled_Buffer controlled_buffer_2
  not not_1 (s1, controlled_buffer_2_out);
endmodule

module CA1 (
  input  [7:0] X,
  output [7:0] not_X
);

  assign not_X = ~X;  // NOT_Gate not_1, 8 bits wide
endmodule

module MultiplicadorBit (
  input  [7:0] X,
  input  z,
  output [7:0] X___z
);

  and and_1 (X___z[0], X[0], z);
  and and_2 (X___z[1], X[1], z);
  and and_3 (X___z[2], X[2], z);
  and and_4 (X___z[3], X[3], z);
  and and_5 (X___z[4], X[4], z);
  and and_6 (X___z[5], X[5], z);
  and and_7 (X___z[6], X[6], z);
  and and_8 (X___z[7], X[7], z);
endmodule

module Semisumador (
  input  w,
  input  x,
  output w___x,
  output carry
);

  xor xor_1 (w___x, w, x);
  and and_1 (carry, w, x);
endmodule

module SumTot8 (
  input  [7:0] X,
  input  [7:0] W,
  output out_3,
  output [7:0] out_4
);

  wire sumtot2_2_c_f, sumtot2_3_c_f, sumtot2_4_c_f, sumtot2_5_c_f, sumtot2_6_c_f, sumtot2_7_c_f,
       sumtot2_8_c_f;

  SumTot2 sumtot2_1 (.c_0(sumtot2_2_c_f), .w(W[7]), .x(X[7]), .S(out_4[7]), .c_f(out_3));
  SumTot2 sumtot2_2 (.c_0(sumtot2_4_c_f), .w(W[6]), .x(X[6]), .S(out_4[6]), .c_f(sumtot2_2_c_f));
  SumTot2 sumtot2_3 (.c_0(sumtot2_5_c_f), .w(W[4]), .x(X[4]), .S(out_4[4]), .c_f(sumtot2_3_c_f));
  SumTot2 sumtot2_4 (.c_0(sumtot2_3_c_f), .w(W[5]), .x(X[5]), .S(out_4[5]), .c_f(sumtot2_4_c_f));
  SumTot2 sumtot2_5 (.c_0(sumtot2_6_c_f), .w(W[3]), .x(X[3]), .S(out_4[3]), .c_f(sumtot2_5_c_f));
  SumTot2 sumtot2_6 (.c_0(sumtot2_7_c_f), .w(W[2]), .x(X[2]), .S(out_4[2]), .c_f(sumtot2_6_c_f));
  SumTot2 sumtot2_7 (.c_0(sumtot2_8_c_f), .w(W[1]), .x(X[1]), .S(out_4[1]), .c_f(sumtot2_7_c_f));
  SumTot2 sumtot2_8 (.c_0(1'b0), .w(W[0]), .x(X[0]), .S(out_4[0]), .c_f(sumtot2_8_c_f));

  // Notes on the sheet:
  //   X + W
endmodule

module SumTot2 (
  input  c_0,
  input  w,
  input  x,
  output S,
  output c_f
);

  wire semisumador_1_carry, semisumador_1_w___x, semisumador_2_carry;

  Semisumador semisumador_1 (.w(w), .x(x), .w___x(semisumador_1_w___x), .carry(semisumador_1_carry));
  Semisumador semisumador_2 (.w(semisumador_1_w___x), .x(c_0), .w___x(S), .carry(semisumador_2_carry));
  or or_1 (c_f, semisumador_2_carry, semisumador_1_carry);
endmodule

module CA1___mult___sum (
  input  in_1,
  input  in_2,
  input  Z,
  input  [7:0] X,
  input  [7:0] W,
  output out_6,
  output out_7,
  output out_8,
  output out_9,
  output out_10,
  output out_11,
  output out_12,
  output out_13,
  output out_14,
  output out_15,
  output out_16,
  output out_17,
  output out_18,
  output out_19,
  output out_20,
  output out_21,
  output out_22,
  output out_23
);

  wire and_1_out, and_2_out, and_3_out, controlled_buffer_3_out, or_1_out, W___X_out_3;
  wire [7:0] CA1_not_x, controlled_buffer_1_out, W___X_out_4, X___Z_x___z;

  and and_1 (and_1_out, in_2, in_1);
  and and_2 (and_2_out, in_2, ~in_1);  // AND_Gate
  and and_3 (and_3_out, ~in_2, in_1);  // AND_Gate
  SumTot8 W___X (.X(X), .W(W), .out_3(W___X_out_3), .out_4(W___X_out_4));
  CA1 CA1 (.X(X), .not_X(CA1_not_x));
  assign controlled_buffer_1_out = and_2_out ? CA1_not_x : 8'bz;  // Controlled_Buffer controlled_buffer_1
  MultiplicadorBit X___Z (.X(X), .z(Z), .X___z(X___Z_x___z));
  assign controlled_buffer_1_out = and_3_out ? X___Z_x___z : 8'bz;  // Controlled_Buffer controlled_buffer_2
  assign controlled_buffer_3_out = and_1_out ? W___X_out_3 : 1'bz;  // Controlled_Buffer controlled_buffer_3
  assign controlled_buffer_1_out = and_1_out ? W___X_out_4 : 8'bz;  // Controlled_Buffer controlled_buffer_4
  or or_1 (or_1_out, and_1_out, and_2_out, and_3_out);
  led led_1 (.a(controlled_buffer_1_out[7]), .encendido___apagado(or_1_out), .s2(out_9), .s1(out_8));
  led led_2 (.a(controlled_buffer_3_out), .encendido___apagado(and_1_out), .s2(out_7), .s1(out_6));
  led led_3 (.a(controlled_buffer_1_out[6]), .encendido___apagado(or_1_out), .s2(out_11), .s1(out_10));
  led led_4 (.a(controlled_buffer_1_out[5]), .encendido___apagado(or_1_out), .s2(out_13), .s1(out_12));
  led led_5 (.a(controlled_buffer_1_out[4]), .encendido___apagado(or_1_out), .s2(out_15), .s1(out_14));
  led led_6 (.a(controlled_buffer_1_out[3]), .encendido___apagado(or_1_out), .s2(out_17), .s1(out_16));
  led led_7 (.a(controlled_buffer_1_out[2]), .encendido___apagado(or_1_out), .s2(out_19), .s1(out_18));
  led led_8 (.a(controlled_buffer_1_out[1]), .encendido___apagado(or_1_out), .s2(out_21), .s1(out_20));
  led led_9 (.a(controlled_buffer_1_out[0]), .encendido___apagado(or_1_out), .s2(out_23), .s1(out_22));

  // Notes on the sheet:
  //   0 0: indiferente
  //   0 1: CA1 (X)
  //   Referencias (c0 / c1): 
  //   1 0: multiplicadorbit (X * Z)
  //   1 1: sumtot8 (W + X)
  //   LEDs
endmodule
