// Logisim project ejerB.circ as structural Verilog: 6 circuits, main circuit main
module main (
  input  x3,
  input  x2,
  input  x1,
  input  x0,
  input  y3,
  input  y2,
  input  y1,
  input  y0,
  output [7:0] out_9,
  output [2:0] out_10,
  output [7:0] out_11,
  output [2:0] out_12
);

  wire and_3_out, and_6_out, and_7_out, and_8_out, and_9_out, and_10_out, and_11_out, and_12_out, and_13_out,
       and_14_out, and_15_out, and_16_out, and_17_out, Ck_out,
       \contador_0_6_modificado_control_multiplicación_1_cargar_datos___desplazar_multiplicador ,
       \contador_0_6_modificado_control_multiplicación_1_correr_a_la_derecha ,
       \contador_0_6_modificado_control_multiplicación_1_mover_a_registro_para_sumar ,
       \contador_0_6_modificado_control_multiplicación_1_reinsertar_resultado ,
       \contador_0_6_modificado_control_multiplicación_1_suma_y_multiplicación ,
       \contador_1_4_memorización_resultado_1_memorizar , d_ff_1_q, Enter_out, j_k_ff_1_qn, or_1_out,
       or_2_out, shift_register_1_out, shift_register_2_out, shift_register_3_q0, shift_register_3_q1,
       shift_register_3_q2, shift_register_3_q3, shift_register_4_out, sum_tot_1_bit_1_c, sum_tot_1_bit_1_s;
  wire [3:0] and_4_out, register_1_q;
  wire [7:0] controlled_buffer_1_out, r_de_desp_8_bits_modificado_registro_principal_1_s0;

  Button Enter (.out(Enter_out));
  and and_1 (and_4_out[3], Enter_out, x3);
  and and_2 (and_4_out[2], Enter_out, x2);
  Register #(.width(4)) register_1 (.D(and_4_out), .Q(register_1_q), .clk(and_3_out));  // open: en, clr
  and and_3 (and_3_out, Enter_out, and_17_out);
  and and_4 (and_4_out[0], Enter_out, x0);
  and and_5 (and_4_out[1], Enter_out, x1);
  Shift_Register #(.length(4)) shift_register_1 (
    .in(1'b0), .clk(and_7_out), .out(shift_register_1_out),
    .load(\contador_0_6_modificado_control_multiplicación_1_cargar_datos___desplazar_multiplicador ),
    .d0(register_1_q[3]), .d1(register_1_q[2]), .d2(register_1_q[1]), .d3(register_1_q[0]));  // open: shift, clr, q0, q1, q2, q3
  and and_6 (and_6_out, Enter_out, y3);
  and and_7 (and_7_out, and_17_out, or_1_out);
  or or_1 (or_1_out, \contador_0_6_modificado_control_multiplicación_1_cargar_datos___desplazar_multiplicador , \contador_0_6_modificado_control_multiplicación_1_suma_y_multiplicación );
  \Contador_0___6_modificado__control_multiplicación  \contador_0_6_modificado_control_multiplicación_1  (
    .Pa0(Enter_out), .Ck(and_17_out), .out_3(out_10),
    .Mover_a_registro_para_sumar(\contador_0_6_modificado_control_multiplicación_1_mover_a_registro_para_sumar ),
    .\Suma_y_multiplicación (\contador_0_6_modificado_control_multiplicación_1_suma_y_multiplicación ),
    .Reinsertar_resultado(\contador_0_6_modificado_control_multiplicación_1_reinsertar_resultado ),
    .Correr_a_la_derecha(\contador_0_6_modificado_control_multiplicación_1_correr_a_la_derecha ),
    .Cargar_datos___Desplazar_multiplicador(\contador_0_6_modificado_control_multiplicación_1_cargar_datos___desplazar_multiplicador ));
  and and_8 (and_8_out, Enter_out, y1);
  and and_9 (and_9_out, Enter_out, y0);
  and and_10 (and_10_out, Enter_out, y2);
  Shift_Register #(.length(4)) shift_register_2 (
    .in(1'b0),
    .clk(\contador_0_6_modificado_control_multiplicación_1_cargar_datos___desplazar_multiplicador ),
    .out(shift_register_2_out), .load(Enter_out), .d0(and_6_out), .d1(and_10_out), .d2(and_8_out),
    .d3(and_9_out));  // open: shift, clr, q0, q1, q2, q3
  and and_11 (and_11_out, shift_register_1_out, shift_register_2_out);
  Sum_Tot_1_bit sum_tot_1_bit_1 (
    .C0(d_ff_1_q), .A(shift_register_4_out), .B(and_11_out), .C(sum_tot_1_bit_1_c), .S(sum_tot_1_bit_1_s));
  or or_2 (or_2_out, \contador_0_6_modificado_control_multiplicación_1_suma_y_multiplicación , \contador_0_6_modificado_control_multiplicación_1_mover_a_registro_para_sumar );
  D_Flip_Flop d_ff_1 (
    .clk(and_16_out), .D(sum_tot_1_bit_1_c), .Q(d_ff_1_q), .reset(Enter_out));  // open: Qn, preset, en
  and and_12 (and_12_out, \contador_0_6_modificado_control_multiplicación_1_suma_y_multiplicación , and_17_out);
  and and_13 (and_13_out, \contador_0_6_modificado_control_multiplicación_1_correr_a_la_derecha , d_ff_1_q);
  and and_14 (and_14_out, \contador_0_6_modificado_control_multiplicación_1_suma_y_multiplicación , sum_tot_1_bit_1_s);
  and and_15 (and_15_out, and_17_out, or_2_out);
  and and_16 (and_16_out, \contador_0_6_modificado_control_multiplicación_1_suma_y_multiplicación , and_17_out);
  Shift_Register #(.length(4)) shift_register_3 (
    .in(and_14_out), .clk(and_12_out),
    .clr(\contador_0_6_modificado_control_multiplicación_1_cargar_datos___desplazar_multiplicador ),
    .q0(shift_register_3_q0), .q1(shift_register_3_q1), .q2(shift_register_3_q2), .q3(shift_register_3_q3));  // open: shift, out, load, d0, d1, d2, d3
  Shift_Register #(.length(4)) shift_register_4 (
    .in(1'b0), .clk(and_15_out), .out(shift_register_4_out),
    .load(\contador_0_6_modificado_control_multiplicación_1_mover_a_registro_para_sumar ),
    .d0(r_de_desp_8_bits_modificado_registro_principal_1_s0[7]),
    .d1(r_de_desp_8_bits_modificado_registro_principal_1_s0[6]),
    .d2(r_de_desp_8_bits_modificado_registro_principal_1_s0[5]),
    .d3(r_de_desp_8_bits_modificado_registro_principal_1_s0[4]));  // open: shift, clr, q0, q1, q2, q3
  R__de_desp__8_bits_modificado__registro_principal r_de_desp_8_bits_modificado_registro_principal_1 (
    .Hab__entrada(\contador_0_6_modificado_control_multiplicación_1_reinsertar_resultado ),
    .Entrada_en_serie(and_13_out), .out_9(out_9), .e3(shift_register_3_q0), .e2(shift_register_3_q1),
    .e1(shift_register_3_q2), .e0(shift_register_3_q3),
    .s7(r_de_desp_8_bits_modificado_registro_principal_1_s0[7]),
    .s6(r_de_desp_8_bits_modificado_registro_principal_1_s0[6]),
    .s5(r_de_desp_8_bits_modificado_registro_principal_1_s0[5]),
    .s4(r_de_desp_8_bits_modificado_registro_principal_1_s0[4]),
    .s3(r_de_desp_8_bits_modificado_registro_principal_1_s0[3]),
    .s2(r_de_desp_8_bits_modificado_registro_principal_1_s0[2]),
    .s1(r_de_desp_8_bits_modificado_registro_principal_1_s0[1]),
    .s0(r_de_desp_8_bits_modificado_registro_principal_1_s0[0]),
    .Ck(\contador_0_6_modificado_control_multiplicación_1_correr_a_la_derecha ), .Pa0(Enter_out));
  assign controlled_buffer_1_out = \contador_1_4_memorización_resultado_1_memorizar  ? r_de_desp_8_bits_modificado_registro_principal_1_s0 : 8'bz;  // Controlled_Buffer controlled_buffer_1
  \Contador_1___4__memorización_resultado  \contador_1_4_memorización_resultado_1  (
    .Ctrl_cont(\contador_0_6_modificado_control_multiplicación_1_mover_a_registro_para_sumar ),
    .Memorizar(\contador_1_4_memorización_resultado_1_memorizar ), .out_5(out_12), .R(Enter_out),
    .Pa0(Enter_out), .Ck(Ck_out));
  J_K_Flip_Flop j_k_ff_1 (
    .J(\contador_1_4_memorización_resultado_1_memorizar ), .clk(Ck_out), .K(Enter_out), .Qn(j_k_ff_1_qn));  // open: Q, preset, en, reset
  Register register_2 (.D(controlled_buffer_1_out), .Q(out_11), .clk(and_17_out), .clr(Enter_out));  // open: en
  and and_17 (and_17_out, j_k_ff_1_qn, Ck_out);
  Hex_Digit_Display hex_digit_display_1 (.value(out_11[7:4]));  // open: dp
  Hex_Digit_Display hex_digit_display_2 (.value(out_11[3:0]));  // open: dp
  Clock Ck (.out(Ck_out));

  // Notes on the sheet:
  //   Multiplicando
  //   Sumador secuencial
  //   Multiplicador
  //   Multiplicador bit
  //   Entrada de datos
  //   Registro de desplazamiento principal
  //   Resultado
endmodule

module R__de_desp__8_bits_modificado__registro_principal (
  input  e3,
  input  e2,
  input  e1,
  input  e0,
  input  Hab__entrada,
  input  Ck,
  input  Entrada_en_serie,
  input  Pa0,
  output [7:0] out_9,
  output s7,
  output s6,
  output s5,
  output s4,
  output s3,
  output s2,
  output s1,
  output s0
);

  wire and_1_out, and_2_out, and_3_out, and_4_out, and_5_out, and_6_out, and_7_out, and_8_out, or_1_out,
       or_2_out, or_3_out, or_4_out;

  and and_1 (and_1_out, Hab__entrada, e3);
  or or_1 (or_1_out, Pa0, and_2_out);
  and and_2 (and_2_out, Hab__entrada, ~e3);  // AND_Gate
  D__pines_reorientados d_pines_reorientados_1 (
    .Ck(Ck), .D(Entrada_en_serie), .Q(out_9[7]), .Pa1(and_1_out), .Pa0(or_1_out));
  and and_3 (and_3_out, Hab__entrada, e2);
  D__pines_reorientados d_pines_reorientados_2 (.Ck(Ck), .D(out_9[7]), .Q(out_9[6]), .Pa1(and_3_out), .Pa0(or_2_out));
  or or_2 (or_2_out, Pa0, and_4_out);
  and and_4 (and_4_out, Hab__entrada, ~e2);  // AND_Gate
  and and_5 (and_5_out, Hab__entrada, e1);
  or or_3 (or_3_out, Pa0, and_6_out);
  and and_6 (and_6_out, Hab__entrada, ~e1);  // AND_Gate
  D__pines_reorientados d_pines_reorientados_3 (.Ck(Ck), .D(out_9[6]), .Q(out_9[5]), .Pa1(and_5_out), .Pa0(or_3_out));
  and and_7 (and_7_out, Hab__entrada, e0);
  D__pines_reorientados d_pines_reorientados_4 (.Ck(Ck), .D(out_9[5]), .Q(out_9[4]), .Pa1(and_7_out), .Pa0(or_4_out));
  or or_4 (or_4_out, Pa0, and_8_out);
  and and_8 (and_8_out, Hab__entrada, ~e0);  // AND_Gate
  D__pines_reorientados d_pines_reorientados_5 (.Ck(Ck), .D(out_9[4]), .Q(out_9[3]), .Pa0(Pa0));  // open: Pa1
  D__pines_reorientados d_pines_reorientados_6 (.Ck(Ck), .D(out_9[3]), .Q(out_9[2]), .Pa0(Pa0));  // open: Pa1
  D__pines_reorientados d_pines_reorientados_7 (.Ck(Ck), .D(out_9[2]), .Q(out_9[1]), .Pa0(Pa0));  // open: Pa1
  D__pines_reorientados d_pines_reorientados_8 (.Ck(Ck), .D(out_9[1]), .Q(out_9[0]), .Pa0(Pa0));  // open: Pa1

  assign s0 = out_9[0];
  assign s1 = out_9[1];
  assign s2 = out_9[2];
  assign s3 = out_9[3];
  assign s4 = out_9[4];
  assign s5 = out_9[5];
  assign s6 = out_9[6];
  assign s7 = out_9[7];

  // Notes on the sheet:
  //   Entradas en paralelo
  //   Salidas en paralelo
endmodule

// +
module Sum_Tot_1_bit (
  input  C0,
  input  A,
  input  B,
  output C,
  output S
);

  wire and_1_out, and_2_out, and_3_out, xor_1_out;

  and and_1 (and_1_out, A, B);
  and and_2 (and_2_out, C0, B);
  and and_3 (and_3_out, C0, A);
  or or_1 (C, and_1_out, and_2_out, and_3_out);
  xor xor_1 (xor_1_out, A, B);
  xor xor_2 (S, xor_1_out, C0);
endmodule

module \Contador_1___4__memorización_resultado  (
  input  Ctrl_cont,
  input  Pa0,
  input  Ck,
  input  R,
  output [2:0] out_5,
  output Memorizar
);

  wire and_1_out, and_2_out, and_3_out, j_k_ff_1_q, j_k_ff_1_qn, or_1_out;

  and and_1 (and_1_out, Ctrl_cont, j_k_ff_1_qn);
  T_Flip_Flop t_ff_1 (.clk(and_1_out), .T(1'b1), .Q(out_5[0]), .reset(or_1_out));  // open: Qn, preset, en
  or or_1 (or_1_out, Pa0, j_k_ff_1_q);
  and and_2 (and_2_out, 1'b1, out_5[0]);
  and and_3 (and_3_out, and_2_out, out_5[1]);
  T_Flip_Flop t_ff_2 (.clk(and_1_out), .T(and_2_out), .Q(out_5[1]), .reset(or_1_out));  // open: Qn, preset, en
  T_Flip_Flop t_ff_3 (.clk(and_1_out), .T(and_3_out), .Q(out_5[2]), .reset(or_1_out));  // open: Qn, preset, en
  and and_4 (Memorizar, out_5[2], ~out_5[1], out_5[0]);  // AND_Gate
  J_K_Flip_Flop j_k_ff_1 (.J(Memorizar), .clk(Ck), .K(R), .Q(j_k_ff_1_q), .Qn(j_k_ff_1_qn));  // open: preset, en, reset
endmodule

// Cont ppal
module \Contador_0___6_modificado__control_multiplicación  (
  input  Pa0,
  input  Ck,
  output [2:0] out_3,
  output Cargar_datos___Desplazar_multiplicador,
  output Mover_a_registro_para_sumar,
  output \Suma_y_multiplicación ,
  output Reinsertar_resultado,
  output Correr_a_la_derecha
);

  wire and_1_out, and_2_out, and_5_out, and_6_out, and_7_out, and_10_out, or_1_out;

  or or_1 (or_1_out, Pa0, and_10_out);
  and and_1 (and_1_out, 1'b1, out_3[0]);
  T_Flip_Flop t_ff_1 (.clk(Ck), .T(1'b1), .Q(out_3[0]), .reset(or_1_out));  // open: Qn, preset, en
  and and_2 (and_2_out, and_1_out, out_3[1]);
  T_Flip_Flop t_ff_2 (.clk(Ck), .T(and_1_out), .Q(out_3[1]), .reset(or_1_out));  // open: Qn, preset, en
  T_Flip_Flop t_ff_3 (.clk(Ck), .T(and_2_out), .Q(out_3[2]), .reset(or_1_out));  // open: Qn, preset, en
  and and_3 (Cargar_datos___Desplazar_multiplicador, ~out_3[0], ~out_3[1], ~out_3[2]);  // AND_Gate
  and and_4 (Mover_a_registro_para_sumar, out_3[0], ~out_3[1], ~out_3[2]);  // AND_Gate
  and and_5 (and_5_out, ~out_3[0], out_3[1], ~out_3[2]);  // AND_Gate
  and and_6 (and_6_out, out_3[0], out_3[1], ~out_3[2]);  // AND_Gate
  and and_7 (and_7_out, ~out_3[0], ~out_3[1], out_3[2]);  // AND_Gate
  and and_8 (Reinsertar_resultado, out_3[0], ~out_3[1], out_3[2]);  // AND_Gate
  and and_9 (Correr_a_la_derecha, ~out_3[0], out_3[1], out_3[2]);  // AND_Gate
  and and_10 (and_10_out, out_3[0], out_3[1], out_3[2]);
  or or_2 (\Suma_y_multiplicación , and_5_out, and_6_out, and_7_out, Reinsertar_resultado);
endmodule

module D__pines_reorientados (
  input  Pa1,
  input  Ck,
  input  D,
  input  Pa0,
  output Q
);

  D_Flip_Flop d_ff_1 (.clk(Ck), .D(D), .Q(Q), .preset(Pa1), .reset(Pa0));  // open: Qn, en
endmodule
